# Fritzing sketch schematic (saved by Fritzing 0.9.3b)
breadboards: 1

parts:
  Part1 = Arduino Uno (Rev3)
  DS1 = DS18B20 1-Wire Temperature Sensor [part_number=DS18B20]
  R1 = Resistor [tolerance=±5% resistance=4.70k package=THT]

nets:
  N1: Part1.D10_PWM/SS, DS1.DQ, R1.Pin_0
  5V: Part1.5V, DS1.VDD, R1.Pin_1
  GND: Part1.GND, DS1.GND
